# Fritzing sketch ACPhaseControl (saved by Fritzing 0.8.0b)
perfboards: 1

parts:
  R1 = Resistor [tolerance=±5% resistance=15k package=THT]  # not connected
  IC1 = IC, DIP package, 6 pins [chip_label=IC]  # not connected
  R2 = Resistor [tolerance=±5% resistance=15k package=THT]
  M1 = DC Motor
  Q1 = NPN-Transistor [package="TO92 [THT]"]
  IC2 = IC, DIP package, 6 pins [chip_label=IC]
  R3 = Resistor [tolerance=±5% resistance=1.5k package=THT]  # not connected
  R4 = Resistor [tolerance=±5% resistance=220 package=THT]  # not connected
  Part1 = Arduino Uno (Rev3)  # not connected

nets:
  N1: R2.Pin_0, Q1.B, IC2.pin4
  N2: M1.pin_2, Q1.E
